# Fritzing sketch handkontroller (saved by Fritzing 0.9.8b)
stripboards: 1

parts:
  Part1 = Arduino Nano (Rev3.0) (ICSP)
  R1 = Rotary Potentiometer (Small) [maximum_resistance=100kΩ package=THT]
  LCM1602_IIC1 = LCM1602 IIC [part_number="LCM1602 IIC" chip_label="LCM1602 IIC" package="DIP (Dual Inline) [THT]"]
  U1 = LCD-16X2 [package=lcd-16x2_noholes]
  S1 = Pushbutton [package="[THT]"]  # not connected
  J1 = Screw terminal - 2 pins [package=THT]  # not connected
  J2 = Screw terminal - 2 pins [package=THT]  # not connected
  J3 = Screw terminal - 2 pins [package=THT]

nets:
  N1: Part1.RESET, LCM1602_IIC1.GND
  N2: Part1.5V, R1.leg1
  N3: Part1.A7, R1.leg2, LCM1602_IIC1.VCC, J3.pin2
  N4: Part1.A4, LCM1602_IIC1.SCL
  N5: Part1.A3, LCM1602_IIC1.SDA
  N6: Part1.A0, R1.wiper
  VSS: LCM1602_IIC1.VSS, U1.VSS
  VDD: LCM1602_IIC1.VDD, U1.VDD
  N7: LCM1602_IIC1.V0, U1.VO
  N8: LCM1602_IIC1.RS, U1.RS
  N9: LCM1602_IIC1.RW, U1.R_W
  N10: LCM1602_IIC1.E, U1.E
  N11: LCM1602_IIC1.D0, U1.DB0
  N12: LCM1602_IIC1.D1, U1.DB1
  N13: LCM1602_IIC1.D2, U1.DB2
  N14: LCM1602_IIC1.D3, U1.DB3
  N15: LCM1602_IIC1.D4, U1.DB4
  N16: LCM1602_IIC1.D5, U1.DB5
  N17: LCM1602_IIC1.D6, U1.DB6
  N18: LCM1602_IIC1.D7, U1.DB7
  N19: LCM1602_IIC1.A, U1.A
  N20: LCM1602_IIC1.K, U1.K

custom parts:
  LCM1602 IIC: I2C-Module to use a 1602 or 2004 LCD on with the wire.h libory Serial LCD Modul
